// Logisim project Zadanie 1 — kopia.circ as structural Verilog: 14 circuits, main circuit main
module main (
  input  in_1,
  input  in_2,
  input  in_3,
  input  in_4
);

  wire dekoder_1_a, dekoder_1_b, dekoder_1_c, dekoder_1_d, dekoder_1_e, dekoder_1_f, dekoder_1_g;

  dekoder dekoder_1 (
    .x(in_1), .y(in_2), .w(in_3), .z(in_4), .a(dekoder_1_a), .b(dekoder_1_b), .c(dekoder_1_c),
    .d(dekoder_1_d), .e(dekoder_1_e), .f(dekoder_1_f), .g(dekoder_1_g));
  _7_Segment_Display u_7_segment_display_1 (
    .g(dekoder_1_d), .f(dekoder_1_c), .a(dekoder_1_b), .b(dekoder_1_a), .e(dekoder_1_e), .d(dekoder_1_f),
    .c(dekoder_1_g));  // open: dp
endmodule

module a (
  input  x,
  input  y,
  input  w,
  input  z,
  output out_5
);

  wire or_1_out, or_2_out;

  or or_1 (or_1_out, x, ~y, w, ~z);  // OR_Gate
  or or_2 (or_2_out, x, ~y, ~w, z);  // OR_Gate
  and and_1 (out_5, or_1_out, or_2_out);
endmodule

module dekoder (
  input  x,
  input  y,
  input  w,
  input  z,
  output a,
  output b,
  output c,
  output d,
  output e,
  output f,
  output g
);

  a a_1 (.x(x), .y(y), .w(w), .z(z), .out_5(a));
  b b_1 (.x(x), .y(y), .w(w), .z(z), .out_5(b));
  c c_1 (.x(x), .y(y), .w(w), .z(z), .out_5(c));
  d d_1 (.x(x), .y(y), .w(w), .z(z), .out_5(d));
  e e_1 (.x(x), .y(y), .w(w), .z(z), .out_5(e));
  f f_1 (.x(x), .y(y), .w(w), .z(z), .out_5(f));
  g g_1 (.x(x), .y(y), .w(w), .z(z), .out_5(g));
endmodule

module b (
  input  x,
  input  y,
  input  w,
  input  z,
  output out_5
);

  wire or_1_out, or_2_out;

  or or_1 (or_1_out, x, ~y, w, z);  // OR_Gate
  or or_2 (or_2_out, x, y, w, ~z);  // OR_Gate
  and and_1 (out_5, or_1_out, or_2_out);
endmodule

module c (
  input  x,
  input  y,
  input  w,
  input  z,
  output out_5
);

  wire and_1_out, and_2_out, and_3_out;

  and and_1 (and_1_out, ~w, ~z);  // AND_Gate
  and and_2 (and_2_out, y, ~w);  // AND_Gate
  and and_3 (and_3_out, y, ~z);  // AND_Gate
  or or_1 (out_5, x, and_1_out, and_2_out, and_3_out);
endmodule

module d (
  input  x,
  input  y,
  input  w,
  input  z,
  output out_5
);

  wire and_1_out, and_2_out, and_3_out;

  and and_1 (and_1_out, ~y, w);  // AND_Gate
  and and_2 (and_2_out, w, ~z);  // AND_Gate
  and and_3 (and_3_out, y, ~w);  // AND_Gate
  or or_1 (out_5, x, and_1_out, and_2_out, and_3_out);
endmodule

module e (
  input  x,
  input  y,
  input  w,
  input  z,
  output out_5
);

  wire and_1_out, and_2_out;

  and and_1 (and_1_out, ~y, ~z);  // AND_Gate
  and and_2 (and_2_out, w, ~z);  // AND_Gate
  or or_1 (out_5, and_1_out, and_2_out);
endmodule

module f (
  input  x,
  input  y,
  input  w,
  input  z,
  output out_5
);

  wire and_1_out, and_2_out, and_3_out, and_4_out;

  and and_1 (and_1_out, ~y, ~z);  // AND_Gate
  and and_2 (and_2_out, ~y, w);  // AND_Gate
  and and_3 (and_3_out, w, ~z);  // AND_Gate
  and and_4 (and_4_out, y, ~w, z);  // AND_Gate
  or or_1 (out_5, x, and_1_out, and_2_out, and_3_out, and_4_out);
endmodule

module g (
  input  x,
  input  y,
  input  w,
  input  z,
  output out_5
);

  or or_1 (out_5, ~w, z, y, x);  // OR_Gate
endmodule

module Zadanie_2 (
);

  wire and_1_out, clock_1_out, d_ff_1_q, d_ff_1_qn, d_ff_2_q, d_ff_2_qn, d_ff_3_q, d_ff_3_qn, d_ff_4_q,
       d_ff_4_qn, dekoder_1_a, dekoder_1_b, dekoder_1_c, dekoder_1_d, dekoder_1_e, dekoder_1_f, dekoder_1_g;

  Clock clock_1 (.out(clock_1_out));
  D_Flip_Flop d_ff_1 (
    .clk(clock_1_out), .D(d_ff_1_qn), .Q(d_ff_1_q), .Qn(d_ff_1_qn), .reset(and_1_out));  // open: preset, en
  D_Flip_Flop d_ff_2 (
    .clk(d_ff_1_qn), .D(d_ff_2_qn), .Q(d_ff_2_q), .Qn(d_ff_2_qn), .reset(and_1_out));  // open: preset, en
  dekoder dekoder_1 (
    .x(d_ff_4_q), .y(d_ff_3_q), .w(d_ff_2_q), .z(d_ff_1_q), .a(dekoder_1_a), .b(dekoder_1_b),
    .c(dekoder_1_c), .d(dekoder_1_d), .e(dekoder_1_e), .f(dekoder_1_f), .g(dekoder_1_g));
  and and_1 (and_1_out, d_ff_2_q, d_ff_4_q);
  D_Flip_Flop d_ff_3 (
    .clk(d_ff_2_qn), .D(d_ff_3_qn), .Q(d_ff_3_q), .Qn(d_ff_3_qn), .reset(and_1_out));  // open: preset, en
  _7_Segment_Display u_7_segment_display_1 (
    .g(dekoder_1_d), .f(dekoder_1_c), .a(dekoder_1_b), .b(dekoder_1_a), .e(dekoder_1_e), .d(dekoder_1_f),
    .c(dekoder_1_g));  // open: dp
  D_Flip_Flop d_ff_4 (
    .clk(d_ff_3_qn), .D(d_ff_4_qn), .Q(d_ff_4_q), .Qn(d_ff_4_qn), .reset(and_1_out));  // open: preset, en
endmodule

module Przerzutnik_D (
  input  D,
  input  Clock,
  output Q,
  output NotQ
);

  wire nand_1_out, nand_2_out, nand_3_out;

  nand nand_1 (nand_1_out, D, D);
  nand nand_2 (nand_2_out, D, Clock);
  nand nand_3 (nand_3_out, Clock, nand_1_out);
  nand nand_4 (Q, nand_2_out, NotQ);
  nand nand_5 (NotQ, Q, nand_3_out);
endmodule

module Zadanie_3 (
  input  A,
  input  B,
  output S,
  output C
);

  xor xor_1 (S, B, A);
  and and_1 (C, B, A);
endmodule

module Zadanie4 (
  input  A,
  input  B,
  input  Cin,
  output S,
  output C
);

  wire and_1_out, and_2_out, xor_1_out;

  xor xor_1 (xor_1_out, A, B);
  and and_1 (and_1_out, xor_1_out, Cin);
  and and_2 (and_2_out, A, B);
  xor xor_2 (S, xor_1_out, Cin);
  or or_1 (C, and_1_out, and_2_out);
endmodule

module Zadanie_5 (
  input  A,
  input  B,
  input  C
);

  wire dekoder_1_a, dekoder_1_b, dekoder_1_c, dekoder_1_d, dekoder_1_e, dekoder_1_f, dekoder_1_g,
       zadanie4_1_c, zadanie4_1_s, zadanie4_2_c, zadanie4_2_s, zadanie_3_1_s;

  Zadanie_3 zadanie_3_1 (.A(A), .B(B), .S(zadanie_3_1_s), .C(zadanie_3_1_s));
  Zadanie4 zadanie4_1 (.A(A), .B(B), .Cin(zadanie_3_1_s), .S(zadanie4_1_s), .C(zadanie4_1_c));
  Zadanie4 zadanie4_2 (.A(A), .B(B), .Cin(zadanie4_1_c), .S(zadanie4_2_s), .C(zadanie4_2_c));
  dekoder dekoder_1 (
    .x(zadanie4_2_c), .y(zadanie4_2_s), .w(zadanie4_1_s), .z(zadanie_3_1_s), .a(dekoder_1_a),
    .b(dekoder_1_b), .c(dekoder_1_c), .d(dekoder_1_d), .e(dekoder_1_e), .f(dekoder_1_f), .g(dekoder_1_g));
  _7_Segment_Display u_7_segment_display_1 (
    .g(dekoder_1_d), .f(dekoder_1_c), .a(dekoder_1_b), .b(dekoder_1_a), .e(dekoder_1_e), .d(dekoder_1_f),
    .c(dekoder_1_g));  // open: dp
endmodule
